// Logisim project e1p2A.circ as structural Verilog: 1 circuit, main circuit main
module main (
  input  A,
  input  B,
  input  C_in,
  output C_out
);

  wire and_1_out, and_2_out, and_3_out;

  and and_1 (and_1_out, A, B, B);
  and and_2 (and_2_out, B, B, C_in);
  and and_3 (and_3_out, A, C_in);
  or or_1 (C_out, and_1_out, and_2_out, and_3_out);
endmodule
