// Logisim project e1p3A.circ as structural Verilog: 1 circuit, main circuit main
module main (
  input  A,
  input  B,
  input  C_in,
  output C_out
);

  wire nand_1_out, nand_2_out, nand_3_out, nand_4_out, nand_5_out;

  nand nand_1 (nand_1_out, A, B);
  nand nand_2 (nand_2_out, B, C_in);
  nand nand_3 (nand_3_out, A, C_in);
  nand nand_4 (nand_4_out, nand_1_out, nand_2_out);
  nand nand_5 (nand_5_out, nand_4_out, nand_4_out);
  nand nand_6 (C_out, nand_5_out, nand_3_out);
endmodule
