// Logisim project e1p3B.circ as structural Verilog: 1 circuit, main circuit main
module main (
  input  A,
  input  B,
  input  C_in,
  output S
);

  wire nand_1_out, nand_2_out, nand_3_out, nand_4_out, nand_5_out, nand_6_out, nand_7_out, nand_8_out,
       nand_9_out;

  nand nand_1 (nand_1_out, B, B);
  nand nand_2 (nand_2_out, C_in, C_in);
  nand nand_3 (nand_3_out, C_in, B);
  nand nand_4 (nand_4_out, nand_1_out, nand_2_out);
  nand nand_5 (nand_5_out, nand_4_out, nand_3_out);
  nand nand_6 (nand_6_out, A, A);
  nand nand_7 (nand_7_out, nand_5_out, nand_5_out);
  nand nand_8 (nand_8_out, nand_5_out, A);
  nand nand_9 (nand_9_out, nand_6_out, nand_7_out);
  nand nand_10 (S, nand_9_out, nand_8_out);
endmodule
