// Logisim project e1p4.circ as structural Verilog: 1 circuit, main circuit main
module main (
  input  D0,
  input  S0,
  input  D1,
  input  S1,
  input  D2,
  input  D3,
  output Y
);

  wire nand_1_out, nand_2_out, nand_3_out, nand_4_out, nand_5_out, nand_6_out, nand_7_out, nand_8_out,
       nand_9_out, nand_10_out, nand_11_out, nand_12_out, nand_13_out, nand_14_out, nand_15_out, nand_16_out,
       nand_17_out, nand_18_out, nand_19_out, nand_20_out;

  nand nand_1 (nand_1_out, S0, S0);
  nand nand_2 (nand_2_out, S1, S1);
  nand nand_3 (nand_3_out, S1, S1);
  nand nand_4 (nand_4_out, S0, S0);
  nand nand_5 (nand_5_out, nand_1_out, nand_2_out);
  nand nand_6 (nand_6_out, S0, nand_3_out);
  nand nand_7 (nand_7_out, nand_4_out, S1);
  nand nand_8 (nand_8_out, S1, S0);
  nand nand_9 (nand_9_out, nand_5_out, nand_5_out);
  nand nand_10 (nand_10_out, nand_6_out, nand_6_out);
  nand nand_11 (nand_11_out, nand_7_out, nand_7_out);
  nand nand_12 (nand_12_out, nand_8_out, nand_8_out);
  nand nand_13 (nand_13_out, D0, nand_9_out);
  nand nand_14 (nand_14_out, D1, nand_10_out);
  nand nand_15 (nand_15_out, D2, nand_11_out);
  nand nand_16 (nand_16_out, D3, nand_12_out);
  nand nand_17 (nand_17_out, nand_13_out, nand_14_out);
  nand nand_18 (nand_18_out, nand_15_out, nand_16_out);
  nand nand_19 (nand_19_out, nand_17_out, nand_17_out);
  nand nand_20 (nand_20_out, nand_18_out, nand_18_out);
  nand nand_21 (Y, nand_19_out, nand_20_out);
endmodule
